# Fritzing sketch RobotArm_schem (saved by Fritzing 0.9.4)
breadboards: 1

parts:
  Part1 = Arduino Uno (Rev3)
  J1 = Basic Servo
  J2 = Basic Servo
  J3 = Basic Servo
  BAT1 = BC9VPC [package=bc9vpc]
  BAT2 = BC9VPC [package=bc9vpc]
  U1 = JOYSTICK-PSP1000 [package=joystick-psp1000]
  C1 = Electrolytic Capacitor [capacitance=1μF package="0405 [SMD, electrolytic]"]
  R1 = Resistor [tolerance=±5% resistance=220 package="0402 [SMD]"]
  IC1 = H-Bridge [package=THT]
  M2 = Stepper Motor - Bipolar
  S2 = Pushbutton [package="[THT]"]
  R2 = Resistor [tolerance=±5% resistance=220 package="0402 [SMD]"]
  S3 = Pushbutton [package="[THT]"]
  R3 = Resistor [tolerance=±5% resistance=220 package="0402 [SMD]"]
  S4 = SPST Switch [package=switche-dpdt]
  C2 = Electrolytic Capacitor [capacitance=1μF package="0405 [SMD, electrolytic]"]

nets:
  N1: Part1.A0, U1.X
  N2: Part1.A1, U1.Y, C1.-
  N3: Part1.D8, S3.Pin_1, S3.Pin_2
  N4: Part1.D9_PWM, J1.pulse
  N5: Part1.D10_PWM/SS, J2.pulse
  N6: Part1.D11_PWM/MOSI, J3.pulse
  GND: Part1.GND, BAT1.V-, U1.GND, R2.Pin_0, R3.Pin_0
  N7: Part1.D2, IC1.1A
  N8: Part1.D3_PWM, IC1.2A
  N9: Part1.D4, IC1.3A
  N10: Part1.D5_PWM, IC1.4A
  N11: Part1.D7, S2.Pin_1, S2.Pin_2
  N12: Part1.VIN, R1.Pin_1, IC1.1_2EN, IC1.3_4EN, IC1.VCC1
  GND_2: J1.gnd, J2.gnd, J3.gnd, BAT2.V-, IC1.GND1, IC1.GND2, IC1.GND3, IC1.GND4, C2.-
  VCC: J1.vcc, J2.vcc, J3.vcc, BAT2.V+, IC1.VCC2, C2.+
  N13: BAT1.V+, S4.P
  N14: U1.VCC, C1.+, R1.Pin_0, S2.Pin_3, S2.Pin_4, R2.Pin_1, S4.O
  N15: IC1.1Y, M2.A
  N16: IC1.2Y, M2.C
  N17: IC1.3Y, M2.D
  N18: IC1.4Y, M2.B
  N19: S3.Pin_3, S3.Pin_4, R3.Pin_1

notes:
  Robot Arm Circuit
